# Fritzing sketch Music Box (saved by Fritzing 0.9.4)
breadboards: 1

parts:
  元件1 = Arduino Nano (Rev3.0)
  LCD1 = LCD screen  # not connected
  VCC1 = Battery
  U1 = SD_CARD_SOCKET [package=sdcard_4uconn]
  SP1 = SPEAKER [package=pcb_mount_speaker]
  S1 = Round Pushbutton
  S4 = Pushbutton [package="[THT]"]
  S5 = Pushbutton [package="[THT]"]
  S6 = Pushbutton [package="[THT]"]
  R3 = Resistor [tolerance=±5% resistance=220 package="0402 [SMD]"]
  R4 = Resistor [tolerance=±5% resistance=220 package="0402 [SMD]"]
  R5 = Resistor [tolerance=±5% resistance=220 package="0402 [SMD]"]

nets:
  N1: 元件1.GND, VCC1.-, U1.VSS2, SP1.+, R3.Pin_0, R4.Pin_0, R5.Pin_0
  N2: 元件1.D5, SP1.-
  N3: 元件1.D7, S6.Pin_1, S6.Pin_2, R5.Pin_1
  N4: 元件1.D8, S5.Pin_1, S5.Pin_2, R4.Pin_1
  N5: 元件1.D9, S4.Pin_1, S4.Pin_2, R3.Pin_1
  N6: 元件1.D10, U1.DAT2
  N7: 元件1.D11/MOSI, U1.CD
  N8: 元件1.5V, U1.DAT1, S1.leg0, S4.Pin_3, S4.Pin_4, S5.Pin_3, S5.Pin_4, S6.Pin_3, S6.Pin_4
  N9: 元件1.D13/SCK, U1.WP
